# Fritzing sketch tempSensor (saved by Fritzing 0.9.3b)
perfboards: 1

parts:
  Raspberry_Pi_1 = Raspberry Pi 3 [part_number=RPI-3-V1.2]
  DS3 = DS18B20 1-Wire Temperature Sensor [part_number=DS18B20]
  R1 = Resistor [tolerance=±5% resistance=10k package="0402 [SMD]"]  # not connected
  J6 = female pin header, 3 pins [form="♀ (female)"]
  J7 = male pin header, 5 pins [form="♂ (male)"]  # not connected
  J8 = single row smd male pin header, 5 pins [form="♂ (male)"]  # not connected
  J9 = male pin header, 5 pins [form="♂ (male)"]  # not connected
  J10 = female pin header, 3 pins [form="♀ (female)"]  # not connected
  J11 = female alternating pin header, 3 pins [form="♀ (female)"]
  IC1 = IC, DIP package, 16 pins [chip_label=MCP3424]

nets:
  N1: Raspberry_Pi_1.3v3, J11.pin1
  N2: Raspberry_Pi_1.GPIO3, IC1.pin5
  N3: Raspberry_Pi_1.GIPO4, J11.pin2
  N4: Raspberry_Pi_1.GND, J11.pin3, IC1.pin6
  N5: Raspberry_Pi_1.5V, IC1.pin2, IC1.pin3, IC1.pin7
  N6: DS3.GND, J6.pin1
  N7: DS3.DQ, J6.pin2
  N8: DS3.VDD, J6.pin3

notes:
  4 x temp probe,
  Connect to board
  For MOS ICs VDD is the more positive supply voltage and Vss is the more negative supply voltage.
